// Digital circuit antikythera.dig as structural Verilog
module antikythera (
  input  clk
);

  wire A_Enable, ALU_A_Enable, ALU_B_Enable, ALU_CF_Enable, ALU_Cin_Override, ALU_Invert, and_2_out,
       AR_Enable, CF, FR_Enable, IP_Enable, IP_Load, IR0_Select, Memory_Load, Memory_Store, not_1_out, OF,
       or_2_out, R_Enable, SF, ST2_Select, Sub_R_W, Sub_WD, TR_Enable, X_Enable, ZF;
  wire [1:0] ALU_A_In_Select, ALU_B_In_Select, ALU_Select, Mem_Addr_Select, Sub_Select, TR_In_Select;
  wire [3:1] add_and_compare_1_c;
  wire [7:0] A_q, add_and_compare_1_s, ALU_A_q, ALU_B_q, and_1_out, AR_q, IP_out, IR0_q, IR1_q, IR2_q,
       lower_d, multiplexer_1_out, multiplexer_2_out, multiplexer_3_out, multiplexer_4_out,
       multiplexer_5_out, multiplexer_6_out, multiplexer_7_out, multiplexer_8_out, multiplexer_9_out,
       or_1_out, R_q, TR_q, upper_d, X_q, xor_1_out, xor_2_out;

  CounterPreset #(.Bits(8)) IP (
    .en(IP_Enable), .C(clk), .dir(1'b0), .in(multiplexer_9_out), .ld(IP_Load), .clr(1'b0), .out(IP_out));  // open: ovf
  Multiplexer #(.Selector_Bits(2), .Bits(8)) multiplexer_1 (
    .sel(Sub_Select), .in_0({8{1'b0}}), .in_1({{5{1'b0}}, Sub_WD, Sub_R_W, 1'b1}),
    .in_2({{5{1'b0}}, Sub_WD, Sub_R_W, 1'b1}), .in_3({{5{1'b0}}, Sub_WD, Sub_R_W, 1'b1}),
    .out(multiplexer_1_out));
  Register #(.Bits(8)) R (.D(IP_out), .C(clk), .en(R_Enable), .Q(R_q));
  Register #(.Bits(8)) AR (.D(multiplexer_7_out), .C(clk), .en(AR_Enable), .Q(AR_q));
  Multiplexer #(.Bits(8)) multiplexer_2 (
    .sel(IR0_Select), .in_0(multiplexer_7_out), .in_1(multiplexer_1_out), .out(multiplexer_2_out));
  Register #(.Bits(8)) IR0 (.D(multiplexer_2_out), .C(clk), .en(1'b1), .Q(IR0_q));
  Multiplexer #(.Selector_Bits(2), .Bits(8)) multiplexer_3 (
    .sel(TR_In_Select), .in_0(A_q), .in_1(X_q), .in_2(R_q), .in_3(multiplexer_7_out), .out(multiplexer_3_out));
  Multiplexer #(.Selector_Bits(2), .Bits(8)) multiplexer_4 (
    .sel(ALU_A_In_Select), .in_0(A_q), .in_1(X_q), .in_2(IP_out), .in_3(multiplexer_7_out),
    .out(multiplexer_4_out));
  Multiplexer #(.Selector_Bits(2), .Bits(8)) multiplexer_5 (
    .sel(ALU_B_In_Select), .in_0(A_q), .in_1(X_q), .in_2({8{1'b0}}), .in_3(multiplexer_7_out),
    .out(multiplexer_5_out));
  Multiplexer #(.Selector_Bits(2), .Bits(8)) multiplexer_6 (
    .sel(Mem_Addr_Select), .in_0(A_q), .in_1(X_q), .in_2(IP_out), .in_3(AR_q), .out(multiplexer_6_out));
  Register #(.Bits(8)) IR1 (.D(IR0_q), .C(clk), .en(1'b1), .Q(IR1_q));
  ROM #(.AddrBits(7), .Bits(8)) upper (.A(multiplexer_6_out[7:1]), .sel(multiplexer_6_out[0]), .D(upper_d));
  not not_1 (not_1_out, multiplexer_6_out[0]);
  RAMDualPort #(.AddrBits(4), .Bits(8)) lower (
    .A(multiplexer_6_out[7:4]), .Din(multiplexer_9_out), .str(Memory_Store), .C(clk), .ld(Memory_Load),
    .D(lower_d));
  Register #(.Bits(8)) IR2 (.D(IR1_q), .C(clk), .en(1'b1), .Q(IR2_q));
  Register #(.Bits(8)) TR (.D(multiplexer_3_out), .C(clk), .en(TR_Enable), .Q(TR_q));
  Register #(.Bits(8)) ALU_A (.D(multiplexer_4_out), .C(clk), .en(ALU_A_Enable), .Q(ALU_A_q));
  Register #(.Bits(8)) ALU_B (.D(multiplexer_5_out), .C(clk), .en(ALU_B_Enable), .Q(ALU_B_q));
  Multiplexer #(.Bits(8)) multiplexer_7 (.sel(not_1_out), .in_0(upper_d), .in_1(lower_d), .out(multiplexer_7_out));
  assign xor_1_out = ALU_B_q ^ {8{ALU_Invert}};  // XOr xor_1, 8 bits wide
  assign and_1_out = xor_1_out & ALU_A_q;  // And and_1, 8 bits wide
  assign or_1_out = xor_1_out | ALU_A_q;  // Or or_1, 8 bits wide
  assign xor_2_out = xor_1_out ^ ALU_A_q;  // XOr xor_2, 8 bits wide
  add_and_compare add_and_compare_1 (
    .A(ALU_A_q), .B(xor_1_out), .Cin(or_2_out), .S(add_and_compare_1_s), .C(add_and_compare_1_c[1]),
    .O(add_and_compare_1_c[2]), .Z(add_and_compare_1_c[3]));
  or or_2 (or_2_out, ALU_Cin_Override, and_2_out);
  and and_2 (and_2_out, ALU_CF_Enable, CF);
  DipSwitch u_IP_Enable (.out(IP_Enable));
  DipSwitch u_IP_Load (.out(IP_Load));
  DipSwitch u_IR0_Select (.out(IR0_Select));
  DipSwitch Sub_Select_1 (.out(Sub_Select[1]));
  DipSwitch Sub_Select_0 (.out(Sub_Select[0]));
  DipSwitch u_Sub_R_W (.out(Sub_R_W));
  DipSwitch u_Sub_WD (.out(Sub_WD));
  DipSwitch u_AR_Enable (.out(AR_Enable));
  DipSwitch u_Memory_Store (.out(Memory_Store));
  DipSwitch u_Memory_Load (.out(Memory_Load));
  DipSwitch Mem_Addr_Select_1 (.out(Mem_Addr_Select[1]));
  DipSwitch Mem_Addr_Select_0 (.out(Mem_Addr_Select[0]));
  DipSwitch ALU_A_In_Select_1 (.out(ALU_A_In_Select[1]));
  DipSwitch ALU_A_In_Select_0 (.out(ALU_A_In_Select[0]));
  DipSwitch ALU_B_In_Select_1 (.out(ALU_B_In_Select[1]));
  DipSwitch ALU_B_In_Select_0 (.out(ALU_B_In_Select[0]));
  DipSwitch TR_In_Select_1 (.out(TR_In_Select[1]));
  DipSwitch TR_In_Select_0 (.out(TR_In_Select[0]));
  DipSwitch u_ALU_A_Enable (.out(ALU_A_Enable));
  DipSwitch u_ALU_B_Enable (.out(ALU_B_Enable));
  DipSwitch u_TR_Enable (.out(TR_Enable));
  DipSwitch u_ALU_Invert (.out(ALU_Invert));
  DipSwitch u_ALU_Cin_Override (.out(ALU_Cin_Override));
  DipSwitch u_ALU_CF_Enable (.out(ALU_CF_Enable));
  DipSwitch u_FR_Enable (.out(FR_Enable));
  DipSwitch ALU_Select_1 (.out(ALU_Select[1]));
  DipSwitch ALU_Select_0 (.out(ALU_Select[0]));
  DipSwitch u_ST2_Select (.out(ST2_Select));
  DipSwitch u_A_Enable (.out(A_Enable));
  DipSwitch u_X_Enable (.out(X_Enable));
  DipSwitch u_R_Enable (.out(R_Enable));
  Multiplexer #(.Selector_Bits(2), .Bits(8)) multiplexer_8 (
    .sel(ALU_Select), .in_0(and_1_out), .in_1(or_1_out), .in_2(xor_2_out), .in_3(add_and_compare_1_s),
    .out(multiplexer_8_out));
  Multiplexer #(.Bits(8)) multiplexer_9 (
    .sel(ST2_Select), .in_0(TR_q), .in_1(multiplexer_8_out), .out(multiplexer_9_out));
  Register #(.Bits(4)) FR (
    .D({add_and_compare_1_c, add_and_compare_1_s[0]}), .C(clk), .en(FR_Enable), .Q({ZF, OF, CF, SF}));
  Register #(.Bits(8)) A (.D(multiplexer_9_out), .C(clk), .en(A_Enable), .Q(A_q));
  Register #(.Bits(8)) X (.D(multiplexer_9_out), .C(clk), .en(X_Enable), .Q(X_q));

  // Notes on the sheet:
  //   NOP
  //   C
  //   [X]
  //   [C]
  //   ST0
  //   zero
  //   ST1
  //   .
  //   ALU
  //   ST2
  //   use ST1 & result instead
  //   of ST2 & A/B if the ALU is
  //   limiting clock speed rather
  //   than memory
endmodule
